// Logisim project Lab1_4_Bit_Register.circ as structural Verilog: 1 circuit, main circuit main
module main (
  input  _8,
  input  _4,
  input  _2,
  input  _1,
  output out_5,
  output out_6,
  output out_7,
  output _8_2,
  output _4_2,
  output _2_2,
  output _1_2,
  output out_12
);

  wire button_1_out, nand_1_out, nand_2_out, nand_3_out, nand_4_out, nand_5_out, nand_6_out, nand_7_out,
       nand_8_out, nand_9_out, nand_10_out, nand_11_out, nand_12_out;

  Button button_1 (.out(button_1_out));
  nand nand_1 (nand_1_out, _8, button_1_out);
  not nand_2 (nand_2_out, _8);  // NAND_Gate
  nand nand_3 (nand_3_out, nand_2_out, button_1_out);
  nand nand_4 (nand_4_out, _4, button_1_out);
  not nand_5 (nand_5_out, _4);  // NAND_Gate
  nand nand_6 (nand_6_out, nand_5_out, button_1_out);
  nand nand_7 (nand_7_out, _2, button_1_out);
  not nand_8 (nand_8_out, _2);  // NAND_Gate
  nand nand_9 (nand_9_out, nand_8_out, button_1_out);
  nand nand_10 (nand_10_out, _1, button_1_out);
  not nand_11 (nand_11_out, _1);  // NAND_Gate
  nand nand_12 (nand_12_out, nand_11_out, button_1_out);
  nand nand_13 (_8_2, nand_1_out, out_5);
  nand nand_14 (out_5, _8_2, nand_3_out);
  nand nand_15 (_4_2, nand_4_out, out_6);
  nand nand_16 (out_6, _4_2, nand_6_out);
  nand nand_17 (_2_2, nand_7_out, out_7);
  nand nand_18 (out_7, _2_2, nand_9_out);
  nand nand_19 (_1_2, nand_10_out, out_12);
  nand nand_20 (out_12, _1_2, nand_12_out);

  // Notes on the sheet:
  //   Clock
endmodule
